// Logisim project multiplexador.circ as structural Verilog: 1 circuit, main circuit main
module main (
  input  in_1,
  input  in_2,
  input  in_3,
  input  in_4,
  input  in_5,
  input  in_6,
  input  in_7,
  input  in_8,
  input  in_9,
  input  in_10,
  input  in_11,
  input  in_12,
  input  in_13,
  input  in_14,
  input  in_15,
  input  in_16,
  output out_17
);

  wire clock_1_out, multiplexer_1_out, multiplexer_2_out;
  wire [1:0] counter_1_q;
  wire [2:0] counter_1_q_2, counter_1_q_3;

  Multiplexer #(.select(3)) multiplexer_1 (
    .in0(in_1), .in1(in_2), .in2(in_3), .in3(in_4), .in4(in_5), .in5(in_6), .in6(in_7), .in7(in_8),
    .out(multiplexer_1_out), .sel(counter_1_q_2), .en(1'b1));
  Multiplexer #(.select(3)) multiplexer_2 (
    .in0(in_9), .in1(in_10), .in2(in_11), .in3(in_12), .in4(in_13), .in5(in_14), .in6(in_15), .in7(in_16),
    .out(multiplexer_2_out), .sel(counter_1_q_3), .en(1'b1));
  Counter counter_1 (
    .Q({counter_1_q_3[0], counter_1_q_3[1], counter_1_q_3[2], counter_1_q_2[0], counter_1_q_2[1], counter_1_q_2[2], counter_1_q}),
    .clk(clock_1_out));  // open: load, D, count, carry, clr
  Clock clock_1 (.out(clock_1_out));
  Multiplexer #(.select(3)) multiplexer_3 (
    .in0(multiplexer_1_out), .in1(multiplexer_1_out), .in2(multiplexer_2_out), .in3(multiplexer_2_out),
    .out(out_17), .sel({1'b0, counter_1_q}), .en(1'b1));  // open: in4, in5, in6, in7
endmodule
